# Fritzing sketch Inżynierka (saved by Fritzing 0.9.3b)
breadboards: 1

parts:
  Arduino_Mega_2560 = Arduino Mega ADK (Rev3)
  SILNIK_28-BYJ48_1 = 28BYJ-48 Stepper Motor [part_number=28BYJ-48]
  SILNIK_28-BYJ48_2 = 28BYJ-48 Stepper Motor [part_number=28BYJ-48]
  SILNIK_28-BYJ48_3 = 28BYJ-48 Stepper Motor [part_number=28BYJ-48]
  SILNIK_28-BYJ48_4 = 28BYJ-48 Stepper Motor [part_number=28BYJ-48]
  STEROWNIK_ULN2003_1 = 28BYJ-48 Driver Module [part_number=ULN2003 package=THT]
  STEROWNIK_ULN2003_2 = 28BYJ-48 Driver Module [part_number=ULN2003 package=THT]
  STEROWNIK_ULN2003_3 = 28BYJ-48 Driver Module [part_number=ULN2003 package=THT]
  STEROWNIK_ULN2003_4 = 28BYJ-48 Driver Module [part_number=ULN2003 package=THT]
  Wrzutnik_Monet_CH-923 = Coin Acceptor - 6-Coin version
  PRZYCISK_A = SWITCH-MOMENTARY-2 [package=tactile-pth-12mm]
  PRZYCISK_C = SWITCH-MOMENTARY-2 [package=tactile-pth-12mm]
  PRZYCISK_D = SWITCH-MOMENTARY-2 [package=tactile-pth-12mm]
  PRZYCISK_B = SWITCH-MOMENTARY-2 [package=tactile-pth-12mm]
  LCD_SCREEN_2x16_Z_MAGISTRALA_I2C = LCD1602-I2C
  R1 = Resistor [tolerance=±5% resistance=1k package="0805 [SMD]"]
  R2 = Resistor [tolerance=±5% resistance=1k package="0805 [SMD]"]
  R3 = Resistor [tolerance=±5% resistance=1k package="0805 [SMD]"]
  R4 = Resistor [tolerance=±5% resistance=1k package="0805 [SMD]"]
  R5 = Resistor [tolerance=±5% resistance=1k package="0805 [SMD]"]

nets:
  N1: Arduino_Mega_2560.A0, R4.Pin_1
  N2: Arduino_Mega_2560.A1, R3.Pin_1
  N3: Arduino_Mega_2560.A2, R2.Pin_1
  N4: Arduino_Mega_2560.A3, R1.Pin_1
  N5: Arduino_Mega_2560.D21/SCL, LCD_SCREEN_2x16_Z_MAGISTRALA_I2C.SCL
  5V: Arduino_Mega_2560.5V, STEROWNIK_ULN2003_1.Vmotor, STEROWNIK_ULN2003_2.Vmotor, STEROWNIK_ULN2003_3.Vmotor, STEROWNIK_ULN2003_4.Vmotor, PRZYCISK_A.2, PRZYCISK_C.2, PRZYCISK_D.2, PRZYCISK_B.2, LCD_SCREEN_2x16_Z_MAGISTRALA_I2C.VCC, R5.Pin_0
  GND: Arduino_Mega_2560.GND, STEROWNIK_ULN2003_1.GND, STEROWNIK_ULN2003_2.GND, STEROWNIK_ULN2003_4.GND, Wrzutnik_Monet_CH-923.GND, LCD_SCREEN_2x16_Z_MAGISTRALA_I2C.GND, R1.Pin_0, R2.Pin_0, R3.Pin_0, R4.Pin_0
  N6: Arduino_Mega_2560.D2_PWM, Wrzutnik_Monet_CH-923.SIG, R5.Pin_1
  N7: Arduino_Mega_2560.D22, STEROWNIK_ULN2003_1.IN1
  N8: Arduino_Mega_2560.D23, STEROWNIK_ULN2003_1.IN2
  N9: Arduino_Mega_2560.D24, STEROWNIK_ULN2003_1.IN3
  N10: Arduino_Mega_2560.D25, STEROWNIK_ULN2003_1.IN4
  N11: Arduino_Mega_2560.D26, STEROWNIK_ULN2003_2.IN1
  N12: Arduino_Mega_2560.D27, STEROWNIK_ULN2003_2.IN2
  N13: Arduino_Mega_2560.D28, STEROWNIK_ULN2003_2.IN3
  N14: Arduino_Mega_2560.D29, STEROWNIK_ULN2003_2.IN4
  N15: Arduino_Mega_2560.D30, STEROWNIK_ULN2003_3.IN1
  N16: Arduino_Mega_2560.D31, STEROWNIK_ULN2003_3.IN2
  N17: Arduino_Mega_2560.D32, STEROWNIK_ULN2003_3.IN3
  N18: Arduino_Mega_2560.D33, STEROWNIK_ULN2003_3.IN4
  N19: Arduino_Mega_2560.D34, STEROWNIK_ULN2003_4.IN1
  N20: Arduino_Mega_2560.D35, STEROWNIK_ULN2003_4.IN2
  N21: Arduino_Mega_2560.D36, STEROWNIK_ULN2003_4.IN3
  N22: Arduino_Mega_2560.D37, STEROWNIK_ULN2003_4.IN4
  N23: SILNIK_28-BYJ48_1.blue-pin, STEROWNIK_ULN2003_1.blue-pin
  N24: SILNIK_28-BYJ48_1.pink-pin, STEROWNIK_ULN2003_1.pink-pin
  N25: SILNIK_28-BYJ48_1.yellow-pin, STEROWNIK_ULN2003_1.yellow-pin
  N26: SILNIK_28-BYJ48_1.orange-pin, STEROWNIK_ULN2003_1.orange-pin
  N27: SILNIK_28-BYJ48_1.red-pin, STEROWNIK_ULN2003_1.red-pin
  N28: SILNIK_28-BYJ48_2.blue-pin, STEROWNIK_ULN2003_2.blue-pin
  N29: SILNIK_28-BYJ48_2.pink-pin, STEROWNIK_ULN2003_2.pink-pin
  N30: SILNIK_28-BYJ48_2.yellow-pin, STEROWNIK_ULN2003_2.yellow-pin
  N31: SILNIK_28-BYJ48_2.orange-pin, STEROWNIK_ULN2003_2.orange-pin
  N32: SILNIK_28-BYJ48_2.red-pin, STEROWNIK_ULN2003_2.red-pin
  N33: SILNIK_28-BYJ48_3.blue-pin, STEROWNIK_ULN2003_3.blue-pin
  N34: SILNIK_28-BYJ48_3.pink-pin, STEROWNIK_ULN2003_3.pink-pin
  N35: SILNIK_28-BYJ48_3.yellow-pin, STEROWNIK_ULN2003_3.yellow-pin
  N36: SILNIK_28-BYJ48_3.orange-pin, STEROWNIK_ULN2003_3.orange-pin
  N37: SILNIK_28-BYJ48_3.red-pin, STEROWNIK_ULN2003_3.red-pin
  N38: SILNIK_28-BYJ48_4.blue-pin, STEROWNIK_ULN2003_4.blue-pin
  N39: SILNIK_28-BYJ48_4.pink-pin, STEROWNIK_ULN2003_4.pink-pin
  N40: SILNIK_28-BYJ48_4.yellow-pin, STEROWNIK_ULN2003_4.yellow-pin
  N41: SILNIK_28-BYJ48_4.orange-pin, STEROWNIK_ULN2003_4.orange-pin
  N42: SILNIK_28-BYJ48_4.red-pin, STEROWNIK_ULN2003_4.red-pin

custom parts:
  28BYJ-48 Stepper Motor: Unipolar Stepper Motor 28BYJ-48 Top coil - pink & orange Bottom coil - blue & yellow Common rail - red Connector pins: blue - pink - yellow - orange - red
  28BYJ-48 Driver Module: ULN2003 Driver Module for the 28BYJ-48 Unipolar Stepper Motor LED A - Blue wire - Bottom coil left LED B - Pink wire - Top coil left LED C - Yellow wire - Bottom coil right LED D - Orange wire - Top coil right Common rail - red Connector pins: blue - pink - yellow - orange - red Control pins - IN1 to IN4 Power pins - GND & Vmotor (5-12V) On/Off jumper (if removed, power to motor is cut).
  Coin Acceptor - 6-Coin version: 12V coin acceptor that can handle up to 6 different denominations. Output is either pulse width, serial, or single pin per coin value.
  LCD1602-I2C: A standard character display, usually with 2x16 characters. Comes in many colors with LCM1602 IIC attached.
